# Fritzing sketch fritzing (saved by Fritzing 0.9.3b)
breadboards: 1

parts:
  Raspberry_Pi_B_rev1 = Raspberry Pi B rev1
  SW1 = ENCODER_RGB_CA [package=encoder_led_3]
  RHT1 = Humidity and Temperature Sensor RHT03
  R1 = Resistor [tolerance=±5% resistance=220 package="0805 [SMD]"]
  R3 = Resistor [tolerance=±5% resistance=220 package="0805 [SMD]"]
  R4 = Resistor [tolerance=±5% resistance=220 package="0805 [SMD]"]
  R5 = Resistor [tolerance=±5% resistance=220 package="0805 [SMD]"]

nets:
  5V: Raspberry_Pi_B_rev1.5V, SW1.-B, RHT1.Vcc, RHT1.GND_2, R1.Pin_1
  N1: Raspberry_Pi_B_rev1.GPIO_1, RHT1.Data-signal, R1.Pin_0
  N2: Raspberry_Pi_B_rev1.GPIO_17, R3.Pin_0
  N3: Raspberry_Pi_B_rev1.GPIO_4, R5.Pin_0
  N4: Raspberry_Pi_B_rev1.GND, R4.Pin_0
  N5: SW1.+, R4.Pin_1
  N6: SW1.A, R3.Pin_1
  N7: SW1.B, R5.Pin_1
